# Fritzing sketch 555metronome (saved by Fritzing 0.9.2b)
breadboards: 1

parts:
  U1 = 555 Timer [package="DIP8 [THT]"]
  D1 = Rectifier Diode [part_number=1N4001 package="300 mil [THT]"]
  BAT1 = BC9VPC [package=bc9vpc]
  C1 = Ceramic Capacitor [capacitance="100 nF" package="1206 [SMD, multilayer]"]
  R1 = Resistor [tolerance=±5% resistance=1k package="2010 [SMD]"]
  U2 = 3.5mm Audio Jack [package=audio-jack]  # not connected
  R2 = Rotary Potentiometer (Small) [maximum_resistance=100kΩ package=THT]
  C4 = Capacitor Polarized [part_number="22 uF" package=panasonic_c]
  D2 = Rectifier Diode [part_number=1N4148 package="300 mil [THT]"]
  C2 = Capacitor Polarized [part_number="2.2 uF" package=panasonic_c]
  LED1 = LED - 5mm [color="Red (633nm)" package="5 mm [THT]"]
  R3 = Resistor [tolerance=±5% resistance=330 package=THT]
  R8 = Resistor [tolerance=±5% resistance=10k package=THT]
  R9 = Resistor [tolerance=±5% resistance=1k package=THT]
  C1_2 = Capacitor Polarized [part_number="22 uF" package=panasonic_c]
  R4 = Resistor [tolerance=±5% resistance=1k package="2010 [SMD]"]

nets:
  N1: U1.Ground, BAT1.V-, C1.0, C4.-, LED1.cathode, R9.Pin_1, C1_2.-
  N2: U1.Trigger, U1.Threshold, C4.+, D2.cathode, R3.Pin_0
  N3: U1.Output, R8.Pin_0, R4.Pin_1
  N4: U1.Reset, U1.Vcc_Supply_Voltage, D1.cathode, R1.Pin_1, C1_2.+
  N5: U1.Control_Voltage, C1.1
  N6: U1.Discharge, R1.Pin_0, R2.leg1, R2.wiper, D2.anode
  N7: D1.anode, BAT1.V+
  N8: R2.leg2, R3.Pin_1
  N9: C2.+, R8.Pin_1, R9.Pin_0
  N10: LED1.anode, R4.Pin_0

notes:
  R4 1K
  R5 1K
  R2 10K
  R6 1M
  C3
  (glass/orange)
