# Fritzing sketch Cmoy (saved by Fritzing 0.9.2b)
circuit board: 8.46667cm x 5.64444cm
breadboards: 1

parts:
  BAT1 = BC9VPC [package=bc9vpc]
  R3 = Rotary Potentiometer (Small) [maximum_resistance=10kΩ package=THT]
  J1_INPUT = 3.5mm Audio Jack [package=audio-jack]
  J2_OUTPUT = 3.5mm Audio Jack [package=audio-jack]  # not connected
  R10 = Resistor [tolerance=±5% resistance=1k package="2010 [SMD]"]
  R5 = Resistor [tolerance=±5% resistance=10k package=THT]
  C1 = Capacitor Polarized [part_number="220 uF" package=panasonic_c]
  C2 = Capacitor Polarized [part_number="220 uF" package=panasonic_c]
  C3 = Capacitor Polarized [part_number="220 uF" package=panasonic_c]
  R2 = Resistor [tolerance=±5% resistance=4.7k package="2010 [SMD]"]
  R1 = Resistor [tolerance=±5% resistance=4.7k package="2010 [SMD]"]
  IC1 = Dual Op-Amp [package=dip08]
  C5 = Capacitor [package=cap-pth-small2]
  C4_&_C5 = Capacitor [part_number="0.1 uF FILM (red box)" package=cap-pth-small2]
  R8 = Resistor [tolerance=±5% resistance=100k package="0603 [SMD]"]
  R7 = Rotary Potentiometer (Small) [maximum_resistance=10kΩ package=THT]
  R8_2 = Resistor [tolerance=±5% resistance=100k package="0603 [SMD]"]
  R9 = Resistor [tolerance=±5% resistance=10k package=THT]
  R6 = Resistor [tolerance=±5% resistance=1k package="2010 [SMD]"]

nets:
  N1: BAT1.V+, C1.+, C2.+, R1.Pin_1, IC1.A_V+
  N2: BAT1.V-, C1.-, C3.-, R2.Pin_1, IC1.A_V-
  N3: R3.leg1, R10.Pin_0, C2.-, C3.+, R2.Pin_0, R1.Pin_0, R8.Pin_0, R7.leg1, R8_2.Pin_0, R6.Pin_0
  N4: R3.wiper, C4_&_C5.1
  N5: J1_INPUT.SLEEVE, R7.leg2
  N6: R10.Pin_1, IC1.B_-IN, R9.Pin_0
  N7: R5.Pin_0, IC1.A_OUT
  N8: R5.Pin_1, IC1.A_-IN, IC1.A_+IN, C5.2, R8.Pin_1, R6.Pin_1
  N9: IC1.B_+IN, C4_&_C5.2, R8_2.Pin_1
  N10: IC1.B_OUT, R9.Pin_1
  N11: C5.1, R7.wiper
